# Fritzing sketch glove_dryer (saved by Fritzing 0.9.3b)
breadboards: 1

parts:
  Part1 = Arduino Uno (Rev3)  # not connected
  Part2 = Base Shield V2
  R1 = Resistor [tolerance=±1% resistance=47 package=THT]
  R2 = Resistor [tolerance=±1% resistance=47 package=THT]
  R3 = Resistor [tolerance=±1% resistance=47 package=THT]
  VCC1 = Battery block 9V
  Grove1 = Grove Temperature Sensor
  R5 = Resistor [tolerance=±1% resistance=1k package=THT]
  Q1 = NPN-Transistor [package="TO92 [THT]"]
  M1 = DC Motor
  LED1 = LED - 5mm [color="Red (633nm)" package="5 mm [THT]"]
  LED2 = LED - 5mm [color="Yellow (574nm)" package="5 mm [THT]"]
  LED3 = LED - 5mm [color="Green (565nm)" package="5 mm [THT]"]
  D1 = Rectifier Diode [part_number=1N4001 package="300 mil [THT]"]

nets:
  N1: Part2.GND, VCC1.-, Q1.E, LED1.cathode, LED2.cathode, LED3.cathode, D1.anode
  N2: Part2.D3, R1.Pin_0
  N3: Part2.D4, R2.Pin_0
  N4: Part2.D5, R5.Pin_0
  N5: Part2.D7, R3.Pin_0
  N6: Part2.pin_136, Grove1.GND
  N7: Part2.pin_137, Grove1.VCC
  N8: Part2.pin_139, Grove1.SIG
  N9: R1.Pin_1, LED1.anode
  N10: R2.Pin_1, LED2.anode
  N11: R3.Pin_1, LED3.anode
  N12: VCC1.+, M1.pin_2
  N13: R5.Pin_1, Q1.C
  N14: Q1.B, M1.pin_1, D1.cathode
